# Fritzing sketch MidiControllerSchematic (saved by Fritzing 0.9.3b)
breadboards: 1

parts:
  Teensy_3_1 = Teensy 3.1
  TM1638_Led_and_Key1 = TM1638_Led_and_Key [package=THT]
  U1 = Pololu 2595 [package=so014]
  S1 = Pushbutton [package="[SMD]"]
  S3 = Pushbutton [package="[SMD]"]
  S4 = Pushbutton [package="[SMD]"]
  S5 = Pushbutton [package="[SMD]"]
  S6 = Pushbutton [package="[SMD]"]
  S7 = Pushbutton [package="[SMD]"]
  S8 = Pushbutton [package="[SMD]"]
  S9 = Pushbutton [package="[SMD]"]
  S10 = Pushbutton [package="[SMD]"]
  S11 = Pushbutton [package="[SMD]"]
  S12 = Pushbutton [package="[SMD]"]
  S13 = Pushbutton [package="[SMD]"]
  S14 = Pushbutton [package="[SMD]"]
  S15 = Pushbutton [package="[SMD]"]
  S16 = Pushbutton [package="[SMD]"]
  U2 = GND_CONNECT [package=gnd_connect]

nets:
  GND: Teensy_3_1.GND, TM1638_Led_and_Key1.GND
  N1: Teensy_3_1.D0, U1.A1
  N2: Teensy_3_1.D1, U1.O0
  N3: Teensy_3_1.D2, U1.B0
  N4: Teensy_3_1.D3, Teensy_3_1.D4, Teensy_3_1.D5, Teensy_3_1.D6, Teensy_3_1.D7, Teensy_3_1.D8, Teensy_3_1.D9, Teensy_3_1.D10, Teensy_3_1.D11, Teensy_3_1.D12, Teensy_3_1.A0/D14, Teensy_3_1.A1/D15, Teensy_3_1.A2/D16, Teensy_3_1.A3/D17, Teensy_3_1.A4/D18, S1.Pin_3, S1.Pin_4, S3.Pin_3, S3.Pin_4, S4.Pin_3, S4.Pin_4, S5.Pin_3, S5.Pin_4, S6.Pin_3, S6.Pin_4, S7.Pin_3, S7.Pin_4, S8.Pin_3, S8.Pin_4, S9.Pin_3, S9.Pin_4, S10.Pin_3, S10.Pin_4, S11.Pin_3, S11.Pin_4, S12.Pin_3, S12.Pin_4, S13.Pin_3, S13.Pin_4, S14.Pin_3, S14.Pin_4, S15.Pin_3, S15.Pin_4, S16.Pin_3, S16.Pin_4, U2.DGND
  N5: Teensy_3_1.3V3, U1.A0
  VCC: Teensy_3_1.Vin, TM1638_Led_and_Key1.VCC, U1.VCC
  N6: TM1638_Led_and_Key1.STB, U1.A2
  N7: TM1638_Led_and_Key1.CLK, U1.B2
  N8: TM1638_Led_and_Key1.DIO, U1.O2

notes:
  Please check pinout of polulu - i've just modified an existing part VCCA and VCCB are on the beginning of the board
  upsie

custom parts:
  Pololu 2595: Quad Buffer bi directional 1.5-18.0 V
